# Fritzing sketch gcp (saved by Fritzing 0.9.4)
circuit board: 11.8434cm x 9.45833cm

parts:
  Brew_Light = LED - 3mm [color="Red (633nm)" package="3 mm [THT]"]
  Steam_Light = LED - 3mm [color="Red (633nm)" package="3 mm [THT]"]
  OLED = Adafruit OLED FeatherWing [part_number="Adafruit #2900"]
  PT100_Amplifier = Adafruit MAX31865 RTD Sensor Breakout [part_number="Adafruit #3328"]
  Controller = Adafruit HUZZAH32 ESP32 Feather [part_number="Adafruit #3405"]
  Relay = Screw terminal - 2 pins [package=THT]
  Steam_Light1 = LED - 3mm [color="Red (633nm)" package="3 mm [THT]"]  # not connected

nets:
  N1: Brew_Light.cathode, Steam_Light.cathode, Relay.pin2
  N2: Brew_Light.anode, Controller.IO12_A11
  N3: Steam_Light.anode, Controller.IO13_A12
  N4: OLED.J, Controller.IO15_A8
  N5: OLED.I, Controller.IO32_A7
  N6: OLED.H, Controller.IO14_A6
  N7: PT100_Amplifier.VIN, Controller.VBUS
  GND: PT100_Amplifier.GND, Controller.GND
  N8: PT100_Amplifier.SCLK, Controller.SCK
  N9: PT100_Amplifier.SDO, Controller.MISO
  N10: PT100_Amplifier.SDI, Controller.MOSI
  N11: PT100_Amplifier.CS, Controller.A5_IO4
  N12: Controller.IO27_A10, Relay.pin1

custom parts:
  Adafruit OLED FeatherWing: This is the FeatherWing OLED: it adds a 128x32 monochrome OLED plus 3 user buttons to any Feather main board. These displays are small, only about 1" diagonal, but very readable due to the high contrast of an OLED display. This screen is made of 128x32 individual white OLED pixels and because the display makes its own light, no backlight is required. This reduces the power required to run the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
  Adafruit MAX31865 RTD Sensor Breakout: For precision temperature sensing, nothing beats a Platinum RTD. Resistance temperature detectors (RTDs) are temperature sensors that contain a resistor that changes resistance value as its temperature changes, basically a kind of thermistor. In this sensor, the resistor is actually a small strip of Platinum with a resistance of 100 ohms at 0°C, thus the name PT100. Compared to most NTC/PTC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
